# Fritzing sketch circuit-and-shield (saved by Fritzing 0.9.0b)
circuit board: 5.36514cm x 7.14954cm
breadboards: 1

parts:
  L293D = L293D [package=THT]
  10K = Resistor [tolerance=±5% resistance=10k package=THT]
  1K = Resistor [tolerance=±5% resistance=1k package=THT]
  Q2 = NPN-Transistor [package="TO92 [THT]"]
  1K_2 = Resistor [tolerance=±5% resistance=10k package=THT]
  Stepper = Stepper Motor - Bipolar
  MQ-6 = MQ-6 [part_number=MQ-6]
  1K_3 = Resistor [tolerance=±5% resistance=1k package=THT]
  Part1 = Intel Galileo
  RGB1 = RGB LED (com. cathode, rgb) [package="5 mm [THT]"]
  J1 = Power Jack [package=power_jack_smd]
  Q1 = NPN-Transistor [package="TO92 [THT]"]

nets:
  VCC: L293D.Enable_1, L293D.Enable_2, L293D.+V, 10K.Pin_0, 1K_2.Pin_0, MQ-6.VCC, Part1.5V
  N1: L293D.In_1, 1K.Pin_1, Part1.D5_PWM
  N2: L293D.Out_1_(_Controlled_by_Enable_1_), Stepper.C
  GND: L293D.0V, Q2.E, MQ-6.GND, Part1.GND, J1.GND, Q1.E
  N3: L293D.Out_2_(_Controlled_by_Enable_1_), Stepper.D
  N4: L293D.In_2, 10K.Pin_1, Q1.C
  N5: L293D.+Vmotor, J1.PWR
  N6: L293D.In_3, Q2.C, 1K_2.Pin_1
  N7: L293D.Out_3_(_Controlled_by_Enable_2_), Stepper.B
  N8: L293D.Out_4_(_Controlled_by_Enable_2_), Stepper.A
  N9: L293D.In_4, 1K_3.Pin_0, Part1.D6_PWM
  N10: 1K.Pin_0, Q1.B
  N11: Q2.B, 1K_3.Pin_1
  N12: MQ-6.OUT, Part1.A0
  N13: Part1.D8, RGB1.red_anode
  N14: Part1.D9_PWM, RGB1.common_cathode
  N15: Part1.D10_PWM/SS, RGB1.green_anode
  N16: Part1.D11_PWM/MOSI, RGB1.blue_anode
